# Fritzing sketch GuirlandeDeNoel (saved by Fritzing 0.9.2b)
breadboards: 1

parts:
  Part1 = Arduino Uno (Rev3) - ICSP
  R1 = Resistor [tolerance=±5% resistance=220 package=THT]
  R2 = Resistor [tolerance=±5% resistance=220 package=THT]
  R3 = Resistor [tolerance=±5% resistance=220 package=THT]
  LED1 = smd LED [color="Red (633nm)" package="1206 [SMD]"]
  LED2 = LED - 5mm [color="Red (633nm)" package="5 mm [THT]"]
  LED3 = LED - 5mm [color="Red (633nm)" package="5 mm [THT]"]

nets:
  N1: Part1.D11_PWM/MOSI, LED3.anode
  N2: Part1.D12/MISO, LED2.anode
  N3: Part1.D13/SCK, LED1.anode
  N4: Part1.GND, R1.Pin_0, R2.Pin_0, R3.Pin_0
  N5: R1.Pin_1, LED1.cathode
  N6: R2.Pin_1, LED2.cathode
  N7: R3.Pin_1, LED3.cathode
